# Fritzing sketch preamplificador (saved by Fritzing 0.9.3b)
breadboards: 1

parts:
  R1 = Rotary Potentiometer (Small) [maximum_resistance=100kΩ package=THT]  # not connected
  Componente1 = Arduino Pro Mini v13
  LED1 = RGB LED (com. cathode, rgb) [package="5 mm [THT]"]
  LED2 = RGB LED (com. cathode, rgb) [package="5 mm [THT]"]
  LED3 = RGB LED (com. cathode, rgb) [package="5 mm [THT]"]
  LED4 = RGB LED (com. cathode, rgb) [package="5 mm [THT]"]
  LED5 = LED - 3mm [color="Blue (525nm)" package="3 mm [THT]"]
  LED6 = LED - 3mm [color="Blue (525nm)" package="3 mm [THT]"]
  S1 = Momentary Switch [package=ksa_sealed_tac_switch]  # not connected
  S2 = Momentary Switch [package=ksa_sealed_tac_switch]  # not connected
  U1 = 74HC595 [package="DIP16 [THT]"]
  U2 = 74HC595 [package="DIP16 [THT]"]
  H1 = polarizedheader 4pin 0.156in [package=THT]
  U3 = TLP621 [package=THT]
  U4 = TLP621 [package=THT]
  U5 = TLP621 [package=THT]
  U6 = TLP621 [package=THT]
  IC1 = ADS1015 12-bit ADC Breakout  # not connected
  R3 = Resistor [tolerance=±5% resistance=220 package=THT]

nets:
  N1: Componente1.VCC, LED1.common_cathode
  N2: LED1.red_anode, U1.Q0
  N3: LED1.green_anode, U1.Q1
  N4: LED2.red_anode, U1.Q2
  N5: LED2.green_anode, U1.Q3
  N6: LED3.red_anode, U1.Q4
  N7: LED3.green_anode, U1.Q5
  N8: LED4.red_anode, U1.Q6
  N9: LED4.green_anode, U1.Q7
  N10: LED5.anode, U2.Q4
  N11: LED6.anode, U2.Q5
  N12: U2.Q1, U4.Pin_1
  N13: U2.Q2, U5.Pin_1
  N14: U2.Q3, U6.Pin_1
  N15: U2.GND, R3.Pin_1
  N16: U2.Q0, U3.Pin_1
  N17: H1.pin1, U3.Pin_4
  N18: H1.pin2, U4.Pin_4
  N19: H1.pin3, U5.Pin_4
  N20: H1.pin4, U6.Pin_4
  N21: U3.Pin_2, R3.Pin_0

custom parts:
  ADS1015 12-bit ADC Breakout: ADS1015 12-bit I2C ADC+PGA Breakout
